# Fritzing sketch traffic_light (saved by Fritzing 0.9.3b)
breadboards: 1

parts:
  Parte1 = Arduino Uno (Rev3)
  S1 = Pushbutton [package="[THT]"]
  LED1 = LED - 5mm [color="Red (633nm)" package="5 mm [THT]"]
  LED2 = LED - 5mm [color="Green (565nm)" package="5 mm [THT]"]
  LED3 = LED - 5mm [color="Green (565nm)" package="5 mm [THT]"]
  LED4 = LED - 5mm [color="Yellow (595nm)" package="5 mm [THT]"]
  LED5 = LED - 5mm [color="Red (633nm)" package="5 mm [THT]"]
  R1 = Resistor [tolerance=±5% resistance=10k package=THT]
  R2 = Resistor [tolerance=±5% resistance=10k package=THT]
  R3 = Resistor [tolerance=±5% resistance=10k package=THT]
  R4 = Resistor [tolerance=±5% resistance=10k package=THT]
  R5 = Resistor [tolerance=±5% resistance=10k package=THT]
  R6 = Resistor [tolerance=±5% resistance=10k package=THT]

nets:
  N1: Parte1.GND, R1.Pin_0, R2.Pin_0, R3.Pin_0, R4.Pin_0, R5.Pin_0, R6.Pin_0
  N2: Parte1.D2, S1.Pin_1, S1.Pin_2, R1.Pin_1
  N3: Parte1.D3_PWM, LED1.anode
  N4: Parte1.D4, LED3.anode
  N5: Parte1.D5_PWM, LED2.anode
  N6: Parte1.D6_PWM, LED4.anode
  N7: Parte1.D7, LED5.anode
  N8: Parte1.5V, S1.Pin_3, S1.Pin_4
  N9: LED1.cathode, R2.Pin_1
  N10: LED2.cathode, R3.Pin_1
  N11: LED3.cathode, R4.Pin_1
  N12: LED4.cathode, R5.Pin_1
  N13: LED5.cathode, R6.Pin_1
